# Fritzing sketch board (saved by Fritzing 0.8.3b)
perfboards: 1

parts:
  J1 = single row smd female pin header, 4 pins [form="♀ (female)"]  # not connected
  J2 = female pin header, 4 pins [form="♀ (female)"]
  J3 = female pin header, 6 pins [form="♀ (female)"]
  Atmega1 = attiny85 [package=dip]

nets:
  N1: J2.pin1, Atmega1.Pin_3
  N2: J2.pin4, J3.pin6, Atmega1.Pin_8

notes:
  Tx
  Rx
  Gnd
  Vcc
  Rst
  Sck
  Miso
  Mosi
  Sig
  Ant
